# Fritzing sketch çizim (saved by Fritzing 0.8.7b)
breadboards: 1

parts:
  Eleman1 = Arduino Mega 2560 (Rev3)
  SD_card_module1 = SD Card Module
  Eleman2 = u-blox NEO-6M GPS Breakout
  T1 = LM35 Temperature Sensor [package="TO92 [THT]"]
  SEN1 = Pulse Sensor [package=SIP]

nets:
  N1: Eleman1.A0, SEN1.Signal
  N2: Eleman1.A1, T1.Vout
  N3: Eleman1.D13_PWM, SD_card_module1.SCK
  N4: Eleman1.D12_PWM, SD_card_module1.MISO
  N5: Eleman1.D11_PWM, SD_card_module1.MOSI
  N6: Eleman1.D2_PWM, Eleman2.RXD
  N7: Eleman1.D3_PWM, Eleman2.TXD
  N8: Eleman1.D4_PWM, SD_card_module1.CS
  VCC: Eleman1.5V, SD_card_module1.+5, Eleman2.VCC, T1.+Vs, SEN1.Vcc
  GND: Eleman1.GND, SD_card_module1.GND#0, Eleman2.GND, T1.GND, SEN1.GND

custom parts:
  SD Card Module: SD Card Module Slot Socket Reader For Arduino ARM MCU
  Pulse Sensor: Pulse Sensor Optical Heart Rate Monitor for Arduino and other microcontrollers
