# Fritzing sketch çizim (saved by Fritzing 0.8.7b)
breadboards: 1

parts:
  Eleman1 = Arduino Mega 2560 (Rev3)
  SD_card_module1 = SD Card Module
  Eleman2 = u-blox NEO-6M GPS Breakout
  S6 = PH meter [package=THT]
  T1 = LM35 Temperature Sensor [package="TO92 [THT]"]

nets:
  N1: Eleman1.D13_PWM, SD_card_module1.SCK
  N2: Eleman1.D12_PWM, SD_card_module1.MISO
  N3: Eleman1.D11_PWM, SD_card_module1.MOSI
  N4: Eleman1.D2_PWM, Eleman2.RXD
  N5: Eleman1.D3_PWM, Eleman2.TXD
  N6: Eleman1.D4_PWM, SD_card_module1.CS
  N7: Eleman1.D5_PWM, T1.Vout
  N8: Eleman1.D6_PWM, S6.pin1
  5V: Eleman1.5V, SD_card_module1.+5, Eleman2.VCC, S6.pin3, T1.+Vs
  GND: Eleman1.GND, SD_card_module1.GND#0, Eleman2.GND, S6.pin2, T1.GND

notes:
  Burada lm35 temsili olarak kullanılmış bir komponenttir.
  Kullanılması gereken lm293 kızılötesi hız sensörüne ait çizimler bulunmadığından aynı bacak yapısına uygun lm35 kullanılmıştır.
  ph meter yerine ise dfrobot marka
  Liquid Level Sensor XKC-Y25-T12V SKU SEN0204
  sensör kullanılmalıdır

custom parts:
  SD Card Module: SD Card Module Slot Socket Reader For Arduino ARM MCU
