# Fritzing sketch araç kontrol (saved by Fritzing 0.8.7b)
breadboards: 1

parts:
  SW-1 = Vibration sensor module
  Eleman1 = SRF05 Ultrasonic Rangefinder
  Water_Level_Sensor1 = Water Level Sensor
  Eleman2 = Arduino Uno (Rev3)
  J1 = Piezo Speaker
  R1 = Resistor [tolerance=±5% resistance=220 package=THT]
  U1 = RELAY-2 [package=relay-g5v]

nets:
  VCC: SW-1.vcc, Eleman1.VCC, Water_Level_Sensor1.VCC, Eleman2.5V
  GND: SW-1.Ground, Eleman1.GND, Water_Level_Sensor1.GND, Eleman2.GND, J1.pin1
  N1: SW-1.Digital_output, Eleman2.A1
  N2: Eleman1.Trig, Eleman2.D10_PWM/SS
  N3: Eleman1.Echo, Eleman2.D9_PWM
  N4: Water_Level_Sensor1.SIG, Eleman2.A0
  N5: Eleman2.D12/MISO, U1.5
  N6: Eleman2.D2, R1.Pin_1
  N7: J1.pin2, R1.Pin_0

notes:
  silecekler için + hattı
  silecekler için - hattı

custom parts:
  Vibration sensor module: Single-roller type full induction trigger switch. When no vibration or tilt, the product is ON conduction state, and in the steady state, when a vibration or tilt, the switch will be rendered instantly disconnect the conductive resistance increases, generating a current pulse signal, thereby triggering circuit. The default state of the swith is close Digital output Supply voltage:3.3V-5V On-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
  Water Level Sensor: A water level sensor. This sensor operates at 3V to 5V. The Sig (signal) pin outputs an analogue signal that is in proportion to the amount of water in contact with the sensor.
