# Fritzing sketch çizim (saved by Fritzing 0.8.7b)
breadboards: 1

parts:
  Eleman1 = Arduino Mega 2560 (Rev3)
  SD_card_module1 = SD Card Module
  Eleman2 = u-blox NEO-6M GPS Breakout
  Eleman3 = Adafruit BMP180
  U1 = GAS_SENSOR [package=mq-3]

nets:
  N1: Eleman1.A0, U1.B1
  N2: Eleman1.D21/SCL, Eleman3.SCL
  N3: Eleman1.D20/SDA, Eleman3.SDA
  N4: Eleman1.D13_PWM, SD_card_module1.SCK
  N5: Eleman1.D12_PWM, SD_card_module1.MISO
  N6: Eleman1.D11_PWM, SD_card_module1.MOSI
  3V3: Eleman1.3V3, Eleman3.+3V3
  N7: Eleman1.D2_PWM, Eleman2.RXD
  N8: Eleman1.D3_PWM, Eleman2.TXD
  N9: Eleman1.D4_PWM, SD_card_module1.CS
  5V: Eleman1.5V, SD_card_module1.+5, Eleman2.VCC, U1.A1
  GND: Eleman1.GND, SD_card_module1.GND#0, Eleman2.GND, Eleman3.GND, U1.H1, U1.H2

custom parts:
  SD Card Module: SD Card Module Slot Socket Reader For Arduino ARM MCU
  Adafruit BMP180: This precision sensor from Bosch is the best low-cost sensing solution for measuring barometric pressure and temperature. Because pressure changes with altitude you can also use it as an altimeter! The sensor is soldered onto a PCB with a 3.3V regulator, I2C level shifter and pull-up resistors on the I2C pins. The BMP180 is the next-generation of sensors from Bosch, and replaces the BMP085.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
