# Fritzing sketch gaz-alev-yagmur (saved by Fritzing 0.8.7b)
breadboards: 1

parts:
  Parça1 = Arduino Uno (Rev3)
  R1 = Resistor [tolerance=±5% resistance=330 package="1206 [SMD]"]
  J1 = Piezo Speaker
  Water_Level_Sensor1 = Water Level Sensor
  U1 = GAS_SENSOR [package=mq-3]
  M1 = DC Motor
  Part1 = KY-026 Flame Sensor Module [package="Breakout board"]

nets:
  N1: Parça1.A1, Water_Level_Sensor1.SIG
  N2: Parça1.D4, Part1.D0
  N3: Parça1.D5_PWM, M1.pin_2
  N4: Parça1.D6_PWM, R1.Pin_1
  5V: Parça1.5V, Water_Level_Sensor1.VCC, U1.A1, Part1.+
  GND: Parça1.GND, J1.pin1, Water_Level_Sensor1.GND, U1.B1, M1.pin_1, Part1.G
  N5: R1.Pin_0, J1.pin2

custom parts:
  Water Level Sensor: A water level sensor. This sensor operates at 3V to 5V. The Sig (signal) pin outputs an analogue signal that is in proportion to the amount of water in contact with the sensor.
  KY-026 Flame Sensor Module: KEYES KY-026 Arduino Flame Sensor Module reacts iin the presence of fire.
