# Fritzing sketch sesli güvenlik (saved by Fritzing 0.8.7b)
breadboards: 1

parts:
  Eleman1 = Arduino Uno (Rev3)
  R1 = Photocell (LDR) [package=THT]
  Eleman2 = Humidity Sensor - HIH-4030 Breakout
  R2 = Resistor [tolerance=±5% resistance=220 package=THT]
  M1 = DC Motor
  Eleman3 = Adafruit FONA - Mini Cellular GSM Breakout

nets:
  N1: Eleman1.A0, R2.Pin_1
  N2: Eleman1.D2, Eleman3.RXD_5V
  N3: Eleman1.D3_PWM, Eleman3.TXD_5V
  N4: Eleman1.D4, M1.pin_2
  N5: Eleman1.D5_PWM, Eleman3.SPEAKER2+
  5V: Eleman1.5V, R1.pin_1, Eleman2.VCC
  GND: Eleman1.GND, R1.pin_0, Eleman2.GND, R2.Pin_0, M1.pin_1, Eleman3.GND

custom parts:
  Adafruit FONA - Mini Cellular GSM Breakout: An all-in-one cellular phone module that lets you add voice, text, SMS and GPRS data to your project. Quad-band 850/900/1800/1900MHz - connect onto any global GSM network with any 2G SIM. Includes an onboard LiPoly battery charging circuitry so you can take your project on the go. Also works as an FM radio receiver.
