# Fritzing sketch çizim (saved by Fritzing 0.8.7b)
breadboards: 1

parts:
  Eleman1 = Arduino Mega 2560 (Rev3)
  SD_card_module1 = SD Card Module
  Eleman2 = u-blox NEO-6M GPS Breakout
  Part1 = KY-015 Temperature & Humidity Sensor Module [package="Breakout board"]
  R1 = Photocell (LDR) [package=THT]
  R2 = Resistor [tolerance=±5% resistance=220 package=THT]

nets:
  N1: Eleman1.A1, R1.pin_1, R2.Pin_0
  N2: Eleman1.D13_PWM, SD_card_module1.SCK
  N3: Eleman1.D12_PWM, SD_card_module1.MISO
  N4: Eleman1.D11_PWM, SD_card_module1.MOSI
  GND: Eleman1.GND, SD_card_module1.GND#0, Eleman2.GND, Part1.-, R2.Pin_1
  N5: Eleman1.D2_PWM, Eleman2.RXD
  N6: Eleman1.D3_PWM, Eleman2.TXD
  N7: Eleman1.D4_PWM, SD_card_module1.CS
  N8: Eleman1.D7_PWM, Part1.S
  5V: Eleman1.5V, SD_card_module1.+5, Eleman2.VCC, Part1.Vin, R1.pin_0

custom parts:
  SD Card Module: SD Card Module Slot Socket Reader For Arduino ARM MCU
  KY-015 Temperature & Humidity Sensor Module: KY-015 temperature and humidity sensor module, provides a low-latency serial interface to measure humidity and temperature.
