# Fritzing sketch çizim (saved by Fritzing 0.8.7b)
breadboards: 1

parts:
  Eleman1 = Arduino Mega 2560 (Rev3)
  R1 = Photocell (LDR) [package=THT]
  T1 = LM35 Temperature Sensor [package="TO92 [THT]"]
  R2 = Resistor [tolerance=±5% resistance=10k package=THT]
  SD_card_module1 = SD Card Module
  Eleman2 = u-blox NEO-6M GPS Breakout

nets:
  N1: Eleman1.A0, T1.Vout
  N2: Eleman1.A1, R1.pin_1, R2.Pin_0
  N3: Eleman1.D13_PWM, SD_card_module1.SCK
  N4: Eleman1.D12_PWM, SD_card_module1.MISO
  N5: Eleman1.D11_PWM, SD_card_module1.MOSI
  GND: Eleman1.GND, T1.GND, R2.Pin_1, SD_card_module1.GND#0, Eleman2.GND
  N6: Eleman1.D2_PWM, Eleman2.RXD
  N7: Eleman1.D3_PWM, Eleman2.TXD
  N8: Eleman1.D4_PWM, SD_card_module1.CS
  5V: Eleman1.5V, R1.pin_0, T1.+Vs, SD_card_module1.+5, Eleman2.VCC

custom parts:
  SD Card Module: SD Card Module Slot Socket Reader For Arduino ARM MCU
